# Fritzing sketch 433MHzGPSTracker (saved by Fritzing 0.9.4)

parts:
  U2 = NodeMCU V1.0
  GY-NEO6MV3 = SUP500F [package=sup500f]
  U5 = FS1000A - 433Mhz RF Transmitter [package=THT]
  VCC1 = Battery
  U6 = XD-RF-5V [package=THT]
  ANT1 = Antenna
  VCC2 = Battery  # not connected
  U7 = NodeMCU V1.0

nets:
  N1: U2.D4, U5.DATA
  3V3: U2.3V3, GY-NEO6MV3.TX-O, U5.VCC, VCC1.+
  GND: U2.GND, GY-NEO6MV3.RX-I, U5.GND
  N2: U2.RSV#40, GY-NEO6MV3.VCC
  N3: U2.RSV#41, GY-NEO6MV3.GND
  VCC: U6.VCC, U7.3V3
  N4: U6.DATA, U7.D8
  GND_2: U6.GND, U7.GND
  N5: U6.Attenna, ANT1.antenna_lead

notes:
  GND: Black
  VCC: Red
  RX: Yellow
  TX: Green

custom parts:
  NodeMCU V1.0: ESP8266 based NodeMCU
  FS1000A - 433Mhz RF Transmitter: This is 433Mhz RF transmitter with receiver kit for Arduino ARM MCU wireless Application environment: Remote control switch, receiver module, motorcycles, automobile anti-theft products, home security products, electric doors, shutter doors, windows, remote control socket, remote control LED, remote audio remote control electric doors, garage door remote control, remote control retractable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
  XD-RF-5V: This is 433Mhz RF transmitter with receiver kit for Arduino ARM MCU wireless Application environment: Remote control switch, receiver module, motorcycles, automobile anti-theft products, home security products, electric doors, shutter doors, windows, remote control socket, remote control LED, remote audio remote control electric doors, garage door remote control, remote control retractable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
